// Logisim project s-mips.circ as structural Verilog: 13 circuits, main circuit S-MIPS Board
module S_MIPS_Board (
  input  DESHABILITAR_DISPATCHER,
  output halt
);

  wire button_1_out, CLK, CS, d_ff_1_q, LCLR, LoadRAM, LoadRAMOn, LW, R_R_W, R_W, ram_dispatcher_1_finished,
       RCS, Reset_out, RST, TTY_EN;
  wire [2:0] KDB;
  wire [3:0] LMask, Mask, ram_1_read_time, ram_1_write_time, RMask;
  wire [6:0] KDB_DATA, TTY_DATA;
  wire [15:0] Addr, LAddr, RAddr;
  wire [31:0] I0, I1, I2, I3, LData, ram_1_data_out_0, ram_1_data_out_1, ram_1_data_out_2, ram_1_data_out_3,
       RI0, RI1, RI2, RI3;

  TTY #(.rows(25), .cols(80)) tty_1 (.data(TTY_DATA), .clk(CLK), .we(TTY_EN), .clr(RST));
  not not_1 (LoadRAMOn, ram_dispatcher_1_finished);
  RAM_Dispatcher ram_dispatcher_1 (
    .WriteTime(ram_1_write_time), .Clock(CLK), .Data(LData), .Address(LAddr), .Mask(LMask),
    .Finished(ram_dispatcher_1_finished), .Write(LW), .CLR(LCLR));
  Keyboard #(.buflen(64)) keyboard_1 (.clk(CLK), .re(KDB[0]), .avail(KDB[2]), .data(KDB_DATA));  // open: clr
  RAM ram_1 (
    .Address(RAddr), .Data_Out_0(ram_1_data_out_0), .Data_Out_1(ram_1_data_out_1),
    .Data_Out_2(ram_1_data_out_2), .Data_Out_3(ram_1_data_out_3), .Data_In_0(RI0), .Data_In_1(RI1),
    .Data_In_2(RI2), .Data_In_3(RI3), .Mask(RMask), .nRead_Write(R_R_W), .Chip_Select(RCS),
    .Read_Time(ram_1_read_time), .Reset(button_1_out), .Write_Time(ram_1_write_time));
  Button button_1 (.out(button_1_out));
  D_Flip_Flop d_ff_1 (.clk(CLK), .D(1'b1), .Q(d_ff_1_q), .reset(Reset_out));  // open: Qn, preset, en
  Button Reset (.out(Reset_out));
  S_MIPS s_mips_1 (
    .Kbd_Enable(KDB[0]), .Address(Addr), .Kbd_Clear(KDB[1]), .Kbd_Available(KDB[2]), .RAM_In_0(I0),
    .Kbd_ASCII_Data(KDB_DATA), .RAM_In_1(I1), .TTY_Enable(TTY_EN), .RAM_In_2(I2), .RAM_In_3(I3),
    .TTY_ASCII_Data(TTY_DATA), .Reset(RST), .RAM_Out_0(ram_1_data_out_0), .Clock(CLK),
    .RAM_Out_1(ram_1_data_out_1), .Stop(halt), .RAM_Out_2(ram_1_data_out_2), .RAM_Out_3(ram_1_data_out_3),
    .Mask(Mask), .Read_Time(ram_1_read_time), .Write_Time(ram_1_write_time), .nRead_Write(R_W),
    .Chip_Select(CS));
  D_Flip_Flop d_ff_2 (.clk(CLK), .D(d_ff_1_q), .Qn(LCLR), .reset(Reset_out));  // open: Q, preset, en
  or or_1 (RST, LCLR, LoadRAM);
  Clock clock_1 (.out(CLK));
  Multiplexer #(.width(32), .enable("false")) multiplexer_1 (.in0(I0), .in1(LData), .out(RI0), .sel(LoadRAM));
  Multiplexer #(.width(32), .enable("false")) multiplexer_2 (.in0(I1), .in1(LData), .out(RI1), .sel(LoadRAM));
  Multiplexer #(.width(32), .enable("false")) multiplexer_3 (.in0(I2), .in1(LData), .out(RI2), .sel(LoadRAM));
  Multiplexer #(.width(32), .enable("false")) multiplexer_4 (.in0(I3), .in1(LData), .out(RI3), .sel(LoadRAM));
  and and_1 (LoadRAM, ~DESHABILITAR_DISPATCHER, LoadRAMOn);  // AND_Gate
  Multiplexer #(.width(16), .enable("false")) multiplexer_5 (.in0(Addr), .in1(LAddr), .out(RAddr), .sel(LoadRAM));
  Multiplexer #(.width(4), .enable("false")) multiplexer_6 (.in0(Mask), .in1(LMask), .out(RMask), .sel(LoadRAM));
  Multiplexer #(.enable("false")) multiplexer_7 (.in0(CS), .in1(LW), .out(RCS), .sel(LoadRAM));
  Multiplexer #(.enable("false")) multiplexer_8 (.in0(R_W), .in1(LW), .out(R_R_W), .sel(LoadRAM));

  // Notes on the sheet:
  //   NO MODIFICAR
  //   Keyboard
endmodule

module RAM (
  input  [15:0] Address,
  input  [31:0] Data_In_0,
  input  [31:0] Data_In_1,
  input  [31:0] Data_In_2,
  input  [31:0] Data_In_3,
  input  [3:0] Mask,
  input  nRead_Write,
  input  Chip_Select,
  input  Reset,
  output [31:0] Data_Out_0,
  output [31:0] Data_Out_1,
  output [31:0] Data_Out_2,
  output [31:0] Data_Out_3,
  output [3:0] Read_Time,
  output [3:0] Write_Time
);

  wire and_2_out, and_3_out, and_4_out, and_5_out, and_6_out, and_7_out, and_8_out, and_9_out, Changed, CLK,
       comparator_2_eq, comparator_3_eq, comparator_4_eq, comparator_5_eq, comparator_6_eq, Count,
       demultiplexer_3_out0, Idle, Idle_q, Load, Load0, Load1, nand_1_out, or_1_out, or_2_out, or_3_out,
       or_4_out, or_5_out, or_6_out, or_7_out, or_8_out, or_9_out, or_10_out, Proc_q, Update_Mem, Zero_Time;
  wire [3:0] counter_1_q, multiplexer_1_out, subtractor_1_out;
  wire [31:0] register_1_q, register_2_q, register_3_q, register_4_q, register_5_q;

  // Probe on 4'b0011
  // Probe on 4'b0010
  Multiplexer #(.width(4), .enable("false")) multiplexer_1 (
    .in0(4'b0011), .in1(4'b0010), .out(multiplexer_1_out), .sel(nRead_Write));
  or or_1 (or_1_out, Idle, Update_Mem);
  or or_2 (or_2_out, ~Chip_Select, Reset);  // OR_Gate
  Subtractor #(.width(4)) subtractor_1 (.a(multiplexer_1_out), .b(4'b0010), .out(subtractor_1_out));  // open: bin, bout
  D_Flip_Flop u_Idle (.clk(CLK), .D(or_1_out), .Q(Idle_q), .preset(or_2_out));  // open: Qn, en, reset
  Demultiplexer #(.enable("false")) demultiplexer_1 (.out0(Idle), .out1(Load0), .in(Idle_q), .sel(Changed));
  // Probe on counter_1_q
  Counter #(.width(4), .max('hf)) counter_1 (
    .load(Load), .D(subtractor_1_out), .count(Count), .Q(counter_1_q), .clk(CLK), .clr(or_3_out));  // open: carry
  or or_3 (or_3_out, ~Chip_Select, Reset);  // OR_Gate
  Comparator_part #(.width(4), .mode("unsigned")) comparator_1 (
    .a(4'b0000), .b(counter_1_q), .eq(Zero_Time));  // open: gt, lt
  or or_4 (or_4_out, Count, Load0, Load1);
  Register #(.width(32)) register_1 (.D(Data_In_0), .en(Chip_Select), .Q(register_1_q), .clk(CLK), .clr(or_5_out));
  or or_5 (or_5_out, ~Chip_Select, Reset);  // OR_Gate
  Register #(.width(32)) register_2 (.D(Data_In_1), .en(Chip_Select), .Q(register_2_q), .clk(CLK), .clr(or_6_out));
  or or_6 (or_6_out, ~Chip_Select, Reset);  // OR_Gate
  Register #(.width(32)) register_3 (.D(Data_In_2), .en(Chip_Select), .Q(register_3_q), .clk(CLK), .clr(or_7_out));
  or or_7 (or_7_out, ~Chip_Select, Reset);  // OR_Gate
  Register #(.width(32)) register_4 (.D(Data_In_3), .en(Chip_Select), .Q(register_4_q), .clk(CLK), .clr(or_8_out));
  or or_8 (or_8_out, ~Chip_Select, Reset);  // OR_Gate
  Register #(.width(32)) register_5 (
    .D({{11{1'b1}}, nRead_Write, Mask, Address}), .en(Chip_Select), .Q(register_5_q), .clk(CLK),
    .clr(or_9_out));
  or or_9 (or_9_out, ~Chip_Select, Reset);  // OR_Gate
  D_Flip_Flop Proc (.clk(CLK), .D(or_4_out), .Q(Proc_q), .reset(or_10_out));  // open: Qn, preset, en
  or or_10 (or_10_out, ~Chip_Select, Reset);  // OR_Gate
  Demultiplexer #(.enable("false")) demultiplexer_2 (
    .out0(Count), .out1(Update_Mem), .in(demultiplexer_3_out0), .sel(Zero_Time));
  Demultiplexer #(.enable("false")) demultiplexer_3 (
    .out0(demultiplexer_3_out0), .out1(Load1), .in(Proc_q), .sel(Changed));
  Clock clock_1 (.out(CLK));
  Comparator_part #(.width(32)) comparator_2 (.a(register_1_q), .b(Data_In_0), .eq(comparator_2_eq));  // open: gt, lt
  Comparator_part #(.width(32)) comparator_3 (.a(register_2_q), .b(Data_In_1), .eq(comparator_3_eq));  // open: gt, lt
  Comparator_part #(.width(32)) comparator_4 (.a(register_3_q), .b(Data_In_2), .eq(comparator_4_eq));  // open: gt, lt
  Comparator_part #(.width(32)) comparator_5 (.a(register_4_q), .b(Data_In_3), .eq(comparator_5_eq));  // open: gt, lt
  Comparator_part #(.width(32)) comparator_6 (
    .a(register_5_q), .b({{11{1'b1}}, nRead_Write, Mask, Address}), .eq(comparator_6_eq));  // open: gt, lt
  nand nand_1 (nand_1_out, comparator_6_eq, comparator_2_eq, comparator_3_eq, comparator_4_eq, comparator_5_eq);
  and and_1 (Changed, nand_1_out, Chip_Select);
  or or_11 (Load, Count, Load1, Load0);
  and and_2 (and_2_out, Mask[0], Update_Mem, nRead_Write);
  and and_3 (and_3_out, Mask[1], Update_Mem, nRead_Write);
  and and_4 (and_4_out, Mask[2], Update_Mem, nRead_Write);
  and and_5 (and_5_out, Mask[3], Update_Mem, nRead_Write);
  RAM_part #(.addrWidth(16), .dataWidth(32), .bus("separate")) ram_1 (
    .addr(Address), .din(Data_In_0), .data(Data_Out_0), .str(and_2_out), .sel(Chip_Select), .clk(CLK),
    .ld(and_6_out), .clr(Reset));
  and and_6 (and_6_out, ~nRead_Write, Idle);  // AND_Gate
  RAM_part #(.addrWidth(16), .dataWidth(32), .bus("separate")) ram_2 (
    .addr(Address), .din(Data_In_1), .data(Data_Out_1), .str(and_3_out), .sel(Chip_Select), .clk(CLK),
    .ld(and_7_out), .clr(Reset));
  and and_7 (and_7_out, ~nRead_Write, Idle);  // AND_Gate
  RAM_part #(.addrWidth(16), .dataWidth(32), .bus("separate")) ram_3 (
    .addr(Address), .din(Data_In_2), .data(Data_Out_2), .str(and_4_out), .sel(Chip_Select), .clk(CLK),
    .ld(and_8_out), .clr(Reset));
  and and_8 (and_8_out, ~nRead_Write, Idle);  // AND_Gate
  RAM_part #(.addrWidth(16), .dataWidth(32), .bus("separate")) ram_4 (
    .addr(Address), .din(Data_In_3), .data(Data_Out_3), .str(and_5_out), .sel(Chip_Select), .clk(CLK),
    .ld(and_9_out), .clr(Reset));
  and and_9 (and_9_out, ~nRead_Write, Idle);  // AND_Gate

  assign Read_Time = 4'b0011;
  assign Write_Time = 4'b0010;

  // Other names for the same wires on the sheet: M0 = Mask[0]; M1 = Mask[1]; M2 = Mask[2]; M3 = Mask[3];
  //   RW = nRead_Write; CLR = Reset; CS = Chip_Select; Load2 = Count

  // Notes on the sheet:
  //   NO MODIFICAR
  //   excepto quizás los valores RT y WT
  //   BANK0
  //   BANK1
  //   BANK2
  //   BANK3
endmodule

module S_MIPS (
  input  Kbd_Available,
  input  [6:0] Kbd_ASCII_Data,
  input  [31:0] RAM_Out_0,
  input  [31:0] RAM_Out_1,
  input  Reset,
  input  [31:0] RAM_Out_2,
  input  Clock,
  input  [31:0] RAM_Out_3,
  input  [3:0] Read_Time,
  input  [3:0] Write_Time,
  output Kbd_Enable,
  output [15:0] Address,
  output Kbd_Clear,
  output TTY_Enable,
  output [6:0] TTY_ASCII_Data,
  output Stop,
  output [31:0] RAM_In_0,
  output [31:0] RAM_In_1,
  output [31:0] RAM_In_2,
  output [31:0] RAM_In_3,
  output [3:0] Mask,
  output nRead_Write,
  output Chip_Select
);


  // Other names for the same wires on the sheet: CLK = Clock; CLR = Reset; CS = Chip_Select;
  //   KBD_AVAIL = Kbd_Available; KBD_CLR = Kbd_Clear; KBD_DATA[6:0] = Kbd_ASCII_Data; RAM_A[15:0] = Address;
  //   RAM_INPUT_0[31:0] = RAM_In_0; RAM_INPUT_1[31:0] = RAM_In_1; RAM_INPUT_2[31:0] = RAM_In_2;
  //   RAM_INPUT_3[31:0] = RAM_In_3; RAM_MASK[3:0] = Mask; RAM_OUTPUT_0[31:0] = RAM_Out_0;
  //   RAM_OUTPUT_1[31:0] = RAM_Out_1; RAM_OUTPUT_2[31:0] = RAM_Out_2; RAM_OUTPUT_3[31:0] = RAM_Out_3;
  //   RW = nRead_Write; TTY_DATA[6:0] = TTY_ASCII_Data

  // Notes on the sheet:
  //   RAM ADDRESS
  //   DATA FROM RAM
  //   DATA TO RAM
  //   DATA WRITE MASK
  //   RAM TIMING
  //   RAM CONTROL
  //   KEYBOARD
  //   TTY
  //   SEQUENCING
endmodule

module RAM_Dispatcher (
  input  [3:0] WriteTime,
  input  Clock,
  input  CLR,
  output [31:0] Data,
  output [15:0] Address,
  output [3:0] Mask,
  output Finished,
  output Write
);

  wire demultiplexer_2_out1, demultiplexer_3_out1, End, IDLE_q, IncAddr, Load, or_1_out, or_2_out, While_q,
       WriteEnd;
  wire [3:0] counter_1_q;
  wire [31:0] CurrentAddress_q;

  Counter #(.width(32), .max('hffffffff)) CurrentAddress (
    .count(IncAddr), .Q({CurrentAddress_q[31:18], Address, CurrentAddress_q[1:0]}), .clk(Clock), .clr(CLR));  // open: load, D, carry
  or or_1 (or_1_out, IncAddr, demultiplexer_3_out1, Finished);
  D_Flip_Flop IDLE (.clk(Clock), .D(or_1_out), .Q(IDLE_q), .preset(CLR));  // open: Qn, en, reset
  Demultiplexer #(.enable("false")) demultiplexer_1 (.out0(Load), .out1(Finished), .in(IDLE_q), .sel(End));
  D_Flip_Flop While (.clk(Clock), .D(or_2_out), .Q(While_q), .reset(CLR));  // open: Qn, preset, en
  or or_2 (or_2_out, Write, Load);
  RAM_part #(.addrWidth(18), .dataWidth(32)) ram_1 (
    .addr({Address, CurrentAddress_q[1:0]}), .data(Data), .clk(Clock));  // open: sel, ld, clr
  Demultiplexer #(.enable("false")) demultiplexer_2 (
    .out0(Write), .out1(demultiplexer_2_out1), .in(While_q), .sel(WriteEnd));
  Decoder #(.select(2)) decoder_1 (
    .out0(Mask[0]), .out1(Mask[1]), .out2(Mask[2]), .out3(Mask[3]), .sel(CurrentAddress_q[1:0]));  // open: en
  Demultiplexer #(.enable("false")) demultiplexer_3 (
    .out0(IncAddr), .out1(demultiplexer_3_out1), .in(demultiplexer_2_out1), .sel(End));
  Counter #(.width(4), .max('hf)) counter_1 (
    .load(Load), .D(WriteTime), .count(Write), .Q(counter_1_q), .clk(Clock));  // open: carry, clr
  Comparator_part #(.width(32)) comparator_1 (.a(Data), .b({32{1'b1}}), .eq(End));  // open: gt, lt
  Comparator_part #(.width(4)) comparator_2 (.a(4'b0000), .b(counter_1_q), .eq(WriteEnd));  // open: gt, lt

  // Other names for the same wires on the sheet: CLK = Clock; Count = Write; WT[3:0] = WriteTime
endmodule

module REGISTER_File (
  input  [4:0] DA,
  input  [31:0] DI,
  input  R_W,
  input  [4:0] SA,
  input  [4:0] SB,
  input  Clk,
  input  Reset,
  output [31:0] A,
  output [31:0] B
);

  wire I1, I2, I3, I4, I5, I6, I7, I8, I9, I10, I11, I12, I13, I14, I15, I16, I17, I18, I19, I20, I21, I22,
       I23, I24, I25, I26, I27, I28, I29, I30, I31, I32;
  wire [31:0] O1, O2, O3, O4, O5, O6, O7, O8, O9, O10, O11, O12, O13, O14, O15, O16, O17, O18, O19, O20, O21,
       O22, O23, O24, O25, O26, O27, O28, O29, O30, O31, O32;

  Demultiplexer #(.select(5)) demultiplexer_1 (
    .out0(I1), .out1(I2), .out2(I3), .out3(I4), .out4(I5), .out5(I6), .out6(I7), .out7(I8), .out8(I9),
    .out9(I10), .out10(I11), .out11(I12), .out12(I13), .out13(I14), .out14(I15), .out15(I16), .out16(I17),
    .out17(I18), .out18(I19), .out19(I20), .out20(I21), .out21(I22), .out22(I23), .out23(I24), .out24(I25),
    .out25(I26), .out26(I27), .out27(I28), .out28(I29), .out29(I30), .out30(I31), .out31(I32), .in(R_W),
    .sel(DA));  // open: en
  Register #(.width(32), .trigger("falling")) register_1 (.D(DI), .en(I1), .Q(O1), .clk(Clk), .clr(Reset));
  Register #(.width(32), .trigger("falling")) register_2 (.D(DI), .en(I5), .Q(O5), .clk(Clk), .clr(Reset));
  Register #(.width(32), .trigger("falling")) register_3 (.D(DI), .en(I9), .Q(O9), .clk(Clk), .clr(Reset));
  Register #(.width(32), .trigger("falling")) register_4 (.D(DI), .en(I13), .Q(O13), .clk(Clk), .clr(Reset));
  Register #(.width(32), .trigger("falling")) register_5 (.D(DI), .en(I17), .Q(O17), .clk(Clk), .clr(Reset));
  Register #(.width(32), .trigger("falling")) register_6 (.D(DI), .en(I21), .Q(O21), .clk(Clk), .clr(Reset));
  Register #(.width(32), .trigger("falling")) register_7 (.D(DI), .en(I25), .Q(O25), .clk(Clk), .clr(Reset));
  Register #(.width(32), .trigger("falling")) register_8 (.D(DI), .en(I29), .Q(O29), .clk(Clk), .clr(Reset));
  Register #(.width(32), .trigger("falling")) register_9 (.D(DI), .en(I2), .Q(O2), .clk(Clk), .clr(Reset));
  Register #(.width(32), .trigger("falling")) register_10 (.D(DI), .en(I6), .Q(O6), .clk(Clk), .clr(Reset));
  Register #(.width(32), .trigger("falling")) register_11 (.D(DI), .en(I10), .Q(O10), .clk(Clk), .clr(Reset));
  Register #(.width(32), .trigger("falling")) register_12 (.D(DI), .en(I14), .Q(O14), .clk(Clk), .clr(Reset));
  Register #(.width(32), .trigger("falling")) register_13 (.D(DI), .en(I18), .Q(O18), .clk(Clk), .clr(Reset));
  Register #(.width(32), .trigger("falling")) register_14 (.D(DI), .en(I22), .Q(O22), .clk(Clk), .clr(Reset));
  Register #(.width(32), .trigger("falling")) register_15 (.D(DI), .en(I26), .Q(O26), .clk(Clk), .clr(Reset));
  Register #(.width(32), .trigger("falling")) register_16 (.D(DI), .en(I30), .Q(O30), .clk(Clk), .clr(Reset));
  Register #(.width(32), .trigger("falling")) register_17 (.D(DI), .en(I3), .Q(O3), .clk(Clk), .clr(Reset));
  Register #(.width(32), .trigger("falling")) register_18 (.D(DI), .en(I7), .Q(O7), .clk(Clk), .clr(Reset));
  Register #(.width(32), .trigger("falling")) register_19 (.D(DI), .en(I11), .Q(O11), .clk(Clk), .clr(Reset));
  Register #(.width(32), .trigger("falling")) register_20 (.D(DI), .en(I15), .Q(O15), .clk(Clk), .clr(Reset));
  Register #(.width(32), .trigger("falling")) register_21 (.D(DI), .en(I19), .Q(O19), .clk(Clk), .clr(Reset));
  Register #(.width(32), .trigger("falling")) register_22 (.D(DI), .en(I23), .Q(O23), .clk(Clk), .clr(Reset));
  Register #(.width(32), .trigger("falling")) register_23 (.D(DI), .en(I27), .Q(O27), .clk(Clk), .clr(Reset));
  Register #(.width(32), .trigger("falling")) register_24 (.D(DI), .en(I31), .Q(O31), .clk(Clk), .clr(Reset));
  Register #(.width(32), .trigger("falling")) register_25 (.D(DI), .en(I4), .Q(O4), .clk(Clk), .clr(Reset));
  Register #(.width(32), .trigger("falling")) register_26 (.D(DI), .en(I8), .Q(O8), .clk(Clk), .clr(Reset));
  Register #(.width(32), .trigger("falling")) register_27 (.D(DI), .en(I12), .Q(O12), .clk(Clk), .clr(Reset));
  Register #(.width(32), .trigger("falling")) register_28 (.D(DI), .en(I16), .Q(O16), .clk(Clk), .clr(Reset));
  Register #(.width(32), .trigger("falling")) register_29 (.D(DI), .en(I20), .Q(O20), .clk(Clk), .clr(Reset));
  Register #(.width(32), .trigger("falling")) register_30 (.D(DI), .en(I24), .Q(O24), .clk(Clk), .clr(Reset));
  Register #(.width(32), .trigger("falling")) register_31 (.D(DI), .en(I28), .Q(O28), .clk(Clk), .clr(Reset));
  Register #(.width(32), .trigger("falling")) register_32 (.D(DI), .en(I32), .Q(O32), .clk(Clk), .clr(Reset));
  Multiplexer #(.select(5), .width(32), .enable("false")) multiplexer_1 (
    .in0(O1), .in1(O2), .in2(O3), .in3(O4), .in4(O5), .in5(O6), .in6(O7), .in7(O8), .in8(O9), .in9(O10),
    .in10(O11), .in11(O12), .in12(O13), .in13(O14), .in14(O15), .in15(O16), .in16(O17), .in17(O18),
    .in18(O19), .in19(O20), .in20(O21), .in21(O22), .in22(O23), .in23(O24), .in24(O25), .in25(O26),
    .in26(O27), .in27(O28), .in28(O29), .in29(O30), .in30(O31), .in31(O32), .out(A), .sel(SA));
  Multiplexer #(.select(5), .width(32), .enable("false")) multiplexer_2 (
    .in0(O1), .in1(O2), .in2(O3), .in3(O4), .in4(O5), .in5(O6), .in6(O7), .in7(O8), .in8(O9), .in9(O10),
    .in10(O11), .in11(O12), .in12(O13), .in13(O14), .in14(O15), .in15(O16), .in16(O17), .in17(O18),
    .in18(O19), .in19(O20), .in20(O21), .in21(O22), .in22(O23), .in23(O24), .in24(O25), .in25(O26),
    .in26(O27), .in27(O28), .in28(O29), .in29(O30), .in30(O31), .in31(O32), .out(B), .sel(SB));

  // Other names for the same wires on the sheet: OUT_A[31:0] = A; OUT_B[31:0] = B

  // Notes on the sheet:
  //   Inputs
  //   Data Address
  //   Data In
  //   Read/Write
  //   Selector A
  //   Selector B
  //   Registers
  //   Outputs
  //   Data A
  //   Data B
endmodule

module ALU (
  input  in_1,
  input  in_2,
  input  [31:0] Input,
  input  [31:0] Input_2,
  input  [3:0] in_5,
  output [31:0] Output,
  output [31:0] Output_2,
  output [31:0] Output_3
);

  wire enable, tunnel, tunnel_t;
  wire [31:0] addition, \and , high, low, multiplexer_2_out, multiplexer_3_out, \nand , \nor , \or ,
       remainder, result, slt, subtraction, \xor ;

  assign \and  = Input & Input_2;  // AND_Gate and_1, 32 bits wide
  assign \or  = Input | Input_2;  // OR_Gate or_1, 32 bits wide
  assign \nand  = ~(Input & Input_2);  // NAND_Gate nand_1, 32 bits wide
  assign \nor  = ~(Input | Input_2);  // NOR_Gate nor_1, 32 bits wide
  assign \xor  = Input ^ Input_2;  // XOR_Gate xor_1, 32 bits wide
  Adder #(.width(32)) adder_1 (.a(Input), .b(Input_2), .out(addition));  // open: cin, cout
  Subtractor #(.width(32)) subtractor_1 (.a(Input), .b(Input_2), .out(subtraction));  // open: bin, bout
  Multiplier multiplier_1 (.in_1(Input), .in_2(in_1), .in_3(Input_2), .Output(high), .Output_2(low));
  Divider divider_1 (.in_1(Input), .in_2(in_1), .in_3(Input_2), .out_4(result), .out_5(remainder));
  Comparator comparator_1 (.in_1(Input), .in_2(in_1), .in_3(Input_2), .Output(slt));
  Multiplexer #(.select(4), .width(32), .enable("false")) multiplexer_1 (
    .in0(addition), .in1(subtraction), .in2(slt), .in5(\and ), .in6(\or ), .in7(\nor ), .in8(\xor ),
    .out(Output), .sel(in_5));  // open: in3, in4, in9, in10, in11, in12, in13, in14, in15
  and and_2 (tunnel, ~in_5[0], in_5[1], ~in_5[2], ~in_5[3]);  // AND_Gate
  and and_3 (tunnel_t, in_5[0], in_5[1], ~in_5[2], ~in_5[3]);  // AND_Gate
  or or_2 (enable, tunnel, tunnel_t);
  Multiplexer #(.width(32), .enable("false")) multiplexer_2 (
    .in0(low), .in1(result), .out(multiplexer_2_out), .sel(tunnel_t));
  Multiplexer #(.width(32), .enable("false")) multiplexer_3 (
    .in0(high), .in1(remainder), .out(multiplexer_3_out), .sel(tunnel_t));
  Register #(.width(32)) register_1 (.D(multiplexer_2_out), .en(enable), .Q(Output_2), .clr(in_2));  // open: clk
  Register #(.width(32)) register_2 (.D(multiplexer_3_out), .en(enable), .Q(Output_3), .clr(in_2));  // open: clk

  // Other names for the same wires on the sheet: A[31:0] = Input; B[31:0] = Input_2; clock = in_2;
  //   high_t[31:0] = Output_3; low_t[31:0] = Output_2; _0 = in_5[0]; selector[3:0] = in_5; _1 = in_5[1]; _2 = in_5[2];
  //   _3 = in_5[3]; sign = in_1

  // Notes on the sheet:
  //   ALU
endmodule

module Multiplier (
  input  [31:0] in_1,
  input  in_2,
  input  [31:0] in_3,
  output [31:0] Output,
  output [31:0] Output_2
);

  wire adder_1_cout, adder_3_cout, adder_5_cout, and_1_out, c1, c2, CA, CB;
  wire [31:0] A_2, A_CB, adder_1_out, adder_2_out, adder_3_out, adder_4_out, and_2_out, and_3_out, B_2, B_CA,
       bit_extender_2_out, bit_extender_3_out, C_AB, high, High_X, low, Low_X, multiplier_2_cout,
       multiplier_2_out, shift_left_3_out_3, shift_left_4_out_3, shift_left_5_out_3, shift_left_6_out_3;

  and and_1 (and_1_out, CA, CB);
  assign C_AB = {{31{1'b0}}, and_1_out};  // Bit_Extender bit_extender_1
  assign bit_extender_2_out = {{31{CB}}, CB};  // Bit_Extender bit_extender_2
  assign bit_extender_3_out = {{31{CA}}, CA};  // Bit_Extender bit_extender_3
  Multiplier_part #(.width(32)) multiplier_1 (.a(in_1), .b(in_3), .out(low), .cout(high));  // open: cin
  Shift_Right shift_right_1 (.in_1(in_1), .out_4(A_2), .Output(CA), .in_2(1'b0));
  assign and_2_out = A_2 & bit_extender_2_out;  // AND_Gate and_2, 32 bits wide
  assign and_3_out = B_2 & bit_extender_3_out;  // AND_Gate and_3, 32 bits wide
  Shift_Right shift_right_2 (.in_1(in_3), .out_4(B_2), .Output(CB), .in_2(1'b0));
  Shift_Left shift_left_1 (.in_2(and_2_out), .out_3(A_CB), .in_1(1'b0));  // open: Output
  Shift_Left shift_left_2 (.in_2(and_3_out), .out_3(B_CA), .in_1(1'b0));  // open: Output
  Multiplier_part #(.width(32)) multiplier_2 (
    .a(A_2), .b(B_2), .out(multiplier_2_out), .cout(multiplier_2_cout));  // open: cin
  Shift_Left shift_left_3 (.in_2(multiplier_2_out), .out_3(shift_left_3_out_3), .in_1(1'b0), .Output(c1));
  Shift_Left shift_left_4 (.in_2(multiplier_2_cout), .out_3(shift_left_4_out_3), .in_1(c1));  // open: Output
  Shift_Left shift_left_5 (.in_2(shift_left_3_out_3), .out_3(shift_left_5_out_3), .in_1(1'b0), .Output(c2));
  Shift_Left shift_left_6 (.in_2(shift_left_4_out_3), .out_3(shift_left_6_out_3), .in_1(c2));  // open: Output
  Multiplexer #(.width(32), .enable("false")) multiplexer_1 (.in0(High_X), .in1(high), .out(Output), .sel(in_2));
  Multiplexer #(.width(32), .enable("false")) multiplexer_2 (.in0(Low_X), .in1(low), .out(Output_2), .sel(in_2));
  Adder #(.width(32)) adder_1 (.a(shift_left_5_out_3), .b(A_CB), .out(adder_1_out), .cout(adder_1_cout));  // open: cin
  // Probe on High_X
  Adder #(.width(32)) adder_2 (
    .a(shift_left_6_out_3), .b({32{1'b0}}), .out(adder_2_out), .cin(adder_1_cout));  // open: cout
  Adder #(.width(32)) adder_3 (.a(adder_1_out), .b(B_CA), .out(adder_3_out), .cout(adder_3_cout));  // open: cin
  Adder #(.width(32)) adder_4 (.a(adder_2_out), .b({32{1'b0}}), .out(adder_4_out), .cin(adder_3_cout));  // open: cout
  Adder #(.width(32)) adder_5 (.a(adder_3_out), .b(C_AB), .out(Low_X), .cout(adder_5_cout));  // open: cin
  Adder #(.width(32)) adder_6 (.a(adder_4_out), .b({32{1'b0}}), .out(High_X), .cin(adder_5_cout));  // open: cout

  // Other names for the same wires on the sheet: A[31:0] = in_1; B[31:0] = in_3; sign = in_2

  // Notes on the sheet:
  //   Multiplier
endmodule

module Divider (
  input  [31:0] in_1,
  input  in_2,
  input  [31:0] in_3,
  output [31:0] out_4,
  output [31:0] out_5
);

  wire division, minus_A, minus_B, xor_2_out;
  wire [31:0] A_t, adder_1_out, B_t, division_t_t, multiplexer_4_out, negator_1_out, negator_2_out,
       negator_3_out, negator_4_out, R, rest, subtractor_1_out;

  Negator #(.width(32)) negator_1 (.in(in_1), .out(negator_1_out));
  and and_1 (minus_A, in_1[31], in_2);
  and and_2 (minus_B, in_2, in_3[31]);
  Multiplexer #(.width(32), .enable("false")) multiplexer_1 (.in0(in_1), .in1(negator_1_out), .out(A_t), .sel(minus_A));
  Negator #(.width(32)) negator_2 (.in(in_3), .out(negator_2_out));
  xor xor_1 (division, minus_A, minus_B);
  Negator #(.width(32)) negator_3 (.in(division_t_t), .out(negator_3_out));
  Multiplexer #(.width(32), .enable("false")) multiplexer_2 (.in0(in_3), .in1(negator_2_out), .out(B_t), .sel(minus_B));
  Multiplexer #(.width(32), .enable("false")) multiplexer_3 (
    .in0(division_t_t), .in1(negator_3_out), .out(out_4), .sel(division));
  Divider_part #(.width(32)) divider_1 (.a(A_t), .b(B_t), .out(rest), .rem(R));  // open: upper
  Subtractor #(.width(32)) subtractor_1 (.a(B_t), .b(R), .out(subtractor_1_out));  // open: bin, bout
  Multiplexer #(.width(32), .enable("false")) multiplexer_4 (
    .in0(rest), .in1(adder_1_out), .out(multiplexer_4_out), .sel(minus_A));
  Adder #(.width(32)) adder_1 (.b(32'h1), .out(adder_1_out));  // open: a, cin, cout
  Multiplexer #(.width(32), .enable("false")) multiplexer_5 (
    .in0(R), .in1(subtractor_1_out), .out(out_5), .sel(minus_A));
  Negator #(.width(32)) negator_4 (.in(multiplexer_4_out), .out(negator_4_out));
  Multiplexer #(.width(32), .enable("false")) multiplexer_6 (
    .in0(multiplexer_4_out), .in1(negator_4_out), .out(out_4), .sel(xor_2_out));
  xor xor_2 (xor_2_out, minus_A, minus_B);

  // Other names for the same wires on the sheet: A[31:0] = in_1; B[31:0] = in_3; division_t[31:0] = out_4;
  //   remainder[31:0] = out_5; sign = in_2

  // Notes on the sheet:
  //   Divider
endmodule

module Comparator (
  input  [31:0] in_1,
  input  in_2,
  input  [31:0] in_3,
  output [31:0] Output
);

  wire multiplexer_1_out, slt, sltu;

  Comparator_part #(.width(32)) comparator_1 (.a(in_1), .b(in_3), .lt(slt));  // open: gt, eq
  Comparator_part #(.width(32), .mode("unsigned")) comparator_2 (.a(in_1), .b(in_3), .lt(sltu));  // open: gt, eq
  assign Output = {{31{1'b0}}, multiplexer_1_out};  // Bit_Extender bit_extender_1
  Multiplexer #(.enable("false")) multiplexer_1 (.in0(slt), .in1(sltu), .out(multiplexer_1_out), .sel(in_2));

  // Other names for the same wires on the sheet: A[31:0] = in_1; B[31:0] = in_3; sign = in_2

  // Notes on the sheet:
  //   Comparator
endmodule

module Shift_Right (
  input  [31:0] in_1,
  input  in_2,
  output Output,
  output [31:0] out_4
);


  assign out_4 = {in_2, in_1[31:1]};
  assign Output = in_1[0];

  // Other names for the same wires on the sheet: _2_A[31:0] = {in_2, in_1[31:1]}; A[31:0] = in_1

  // Notes on the sheet:
  //   Shift Right
endmodule

module Shift_Left (
  input  in_1,
  input  [31:0] in_2,
  output [31:0] out_3,
  output Output
);


  assign out_3 = {in_2[30:0], in_1};
  assign Output = in_2[31];

  // Other names for the same wires on the sheet: _2_A[31:0] = {in_2[30:0], in_1}; A[31:0] = in_2

  // Notes on the sheet:
  //   Shift Left
endmodule

module Branch_Control (
  input  [31:0] in_1,
  input  [31:0] in_2,
  input  in_3,
  input  in_4,
  output [31:0] Output
);

  wire and_1_out;
  wire [31:0] multiplexer_1_out;

  and and_1 (and_1_out, in_3, in_4);
  Multiplexer #(.width(32), .enable("false")) multiplexer_1 (
    .in0(in_1), .in1(32'h4), .out(multiplexer_1_out), .sel(and_1_out));
  Adder #(.width(32)) adder_1 (.a(in_2), .b(multiplexer_1_out), .out(Output));  // open: cin, cout

  // Other names for the same wires on the sheet: Flag_Condition = in_4; Instruction_Adress[31:0] = in_2; jmp = in_3;
  //   jump_size[31:0] = in_1

  // Notes on the sheet:
  //   Branch Control
endmodule

module Program_Counter (
  input  [31:0] in_1,
  input  [31:0] in_2,
  input  in_3,
  input  in_4
);

  Register #(.width(32)) register_1 (.D(in_1), .en(in_3), .Q(in_2), .clk(in_4), .clr(1'b0));

  // Other names for the same wires on the sheet: Clk = in_4; Input[31:0] = in_1; Swap = in_3

  // Notes on the sheet:
  //   Output
endmodule
